# Fritzing sketch I2C Hallsensor MCP 23017 (saved by Fritzing 0.9.3b)
circuit board: 8.47cm x 8.5cm
breadboards: 1

parts:
  LED9 = LED - 5mm [color="Red (633nm)" package="5 mm [THT]"]
  330Ω = Resistor [tolerance=±5% resistance=330 package=THT]
  4_7kΩ = Resistor [tolerance=±5% resistance=10k package=THT]
  Q1 = PNP-Transistor [package="TO92 [THT]"]
  I2C_MCP_23017 = MCP23017 I2C I/O Expander
  Q2 = PNP-Transistor [package="TO92 [THT]"]
  LED10 = LED - 5mm [color="Red (633nm)" package="5 mm [THT]"]
  4_7kΩ_2 = Resistor [tolerance=±5% resistance=10k package=THT]
  330Ω_2 = Resistor [tolerance=±5% resistance=330 package=THT]
  Q4 = PNP-Transistor [package="TO92 [THT]"]
  Q3 = PNP-Transistor [package="TO92 [THT]"]
  LED11 = LED - 5mm [color="Red (633nm)" package="5 mm [THT]"]
  LED12 = LED - 5mm [color="Red (633nm)" package="5 mm [THT]"]
  330Ω_3 = Resistor [tolerance=±5% resistance=330 package=THT]
  330Ω_4 = Resistor [tolerance=±5% resistance=330 package=THT]
  1kΩ = Resistor [tolerance=±5% resistance=10k package=THT]
  4_7kΩ_3 = Resistor [tolerance=±5% resistance=10k package=THT]
  Q5 = PNP-Transistor [package="TO92 [THT]"]
  Q8 = PNP-Transistor [package="TO92 [THT]"]
  Q6 = PNP-Transistor [package="TO92 [THT]"]
  Q7 = PNP-Transistor [package="TO92 [THT]"]
  LED16 = LED - 5mm [color="Red (633nm)" package="5 mm [THT]"]
  LED13 = LED - 5mm [color="Red (633nm)" package="5 mm [THT]"]
  LED15 = LED - 5mm [color="Red (633nm)" package="5 mm [THT]"]
  LED14 = LED - 5mm [color="Red (633nm)" package="5 mm [THT]"]
  330Ω_5 = Resistor [tolerance=±5% resistance=330 package=THT]
  330Ω_6 = Resistor [tolerance=±5% resistance=330 package=THT]
  330Ω_7 = Resistor [tolerance=±5% resistance=330 package=THT]
  330Ω_8 = Resistor [tolerance=±5% resistance=330 package=THT]
  4_7kΩ_4 = Resistor [tolerance=±5% resistance=10k package=THT]
  4_7kΩ_5 = Resistor [tolerance=±5% resistance=10k package=THT]
  4_7kΩ_6 = Resistor [tolerance=±5% resistance=10k package=THT]
  4_7kΩ_7 = Resistor [tolerance=±5% resistance=10k package=THT]
  OUT = male pin header, 5 pins [form="♂ (male)"]
  IN = male pin header, 5 pins [form="♂ (male)"]
  A0 = female pin header, 3 pins [form="♀ (female)"]
  A1 = female pin header, 3 pins [form="♀ (female)"]
  A2 = female pin header, 3 pins [form="♀ (female)"]
  10KΩ = Resistor [tolerance=±5% resistance=330 package=THT]
  10KΩ_2 = Resistor [tolerance=±5% resistance=330 package=THT]
  10KΩ_3 = Resistor [tolerance=±5% resistance=330 package=THT]
  Q9 = PNP-Transistor [package="TO92 [THT]"]
  LED1 = LED - 5mm [color="Red (633nm)" package="5 mm [THT]"]
  330Ω_9 = Resistor [tolerance=±5% resistance=330 package=THT]
  4_7kΩ_8 = Resistor [tolerance=±5% resistance=10k package=THT]
  Q10 = PNP-Transistor [package="TO92 [THT]"]
  LED3 = LED - 5mm [color="Red (633nm)" package="5 mm [THT]"]
  330Ω_10 = Resistor [tolerance=±5% resistance=330 package=THT]
  4_7kΩ_9 = Resistor [tolerance=±5% resistance=10k package=THT]
  Q11 = PNP-Transistor [package="TO92 [THT]"]
  LED3_2 = LED - 5mm [color="Red (633nm)" package="5 mm [THT]"]
  330Ω_11 = Resistor [tolerance=±5% resistance=330 package=THT]
  4_7kΩ_10 = Resistor [tolerance=±5% resistance=10k package=THT]
  Q12 = PNP-Transistor [package="TO92 [THT]"]
  LED4 = LED - 5mm [color="Red (633nm)" package="5 mm [THT]"]
  330Ω_12 = Resistor [tolerance=±5% resistance=330 package=THT]
  4_7kΩ_11 = Resistor [tolerance=±5% resistance=10k package=THT]
  Q13 = PNP-Transistor [package="TO92 [THT]"]
  LED5 = LED - 5mm [color="Red (633nm)" package="5 mm [THT]"]
  330Ω_13 = Resistor [tolerance=±5% resistance=330 package=THT]
  4_7kΩ_12 = Resistor [tolerance=±5% resistance=10k package=THT]
  Q14 = PNP-Transistor [package="TO92 [THT]"]
  LED6 = LED - 5mm [color="Red (633nm)" package="5 mm [THT]"]
  330Ω_14 = Resistor [tolerance=±5% resistance=330 package=THT]
  4_7kΩ_13 = Resistor [tolerance=±5% resistance=10k package=THT]
  Q15 = PNP-Transistor [package="TO92 [THT]"]
  LED7 = LED - 5mm [color="Red (633nm)" package="5 mm [THT]"]
  330Ω_15 = Resistor [tolerance=±5% resistance=330 package=THT]
  4_7kΩ_14 = Resistor [tolerance=±5% resistance=10k package=THT]
  Q16 = PNP-Transistor [package="TO92 [THT]"]
  LED8 = LED - 5mm [color="Red (633nm)" package="5 mm [THT]"]
  330Ω_16 = Resistor [tolerance=±5% resistance=330 package=THT]
  4_7kΩ_15 = Resistor [tolerance=±5% resistance=10k package=THT]
  INT = female pin header, 3 pins [form="♀ (female)"]
  10uF = Electrolytic Capacitor [capacitance=1µF package="100 mil [THT, electrolytic]"]
  10nF = Electrolytic Capacitor [capacitance=1µF package="100 mil [THT, electrolytic]"]

nets:
  N1: LED9.cathode, 330Ω.Pin_1
  N2: LED9.anode, 4_7kΩ.Pin_1, Q1.E, I2C_MCP_23017.GPB0
  N3: 330Ω.Pin_0, Q1.B, I2C_MCP_23017.VSS, Q2.B, 330Ω_2.Pin_0, Q4.B, Q3.B, 330Ω_3.Pin_0, 330Ω_4.Pin_0, Q5.B, Q8.B, Q6.B, Q7.B, 330Ω_5.Pin_0, 330Ω_6.Pin_0, 330Ω_7.Pin_0, 330Ω_8.Pin_0, OUT.pin1, IN.pin1, A0.pin3, A1.pin3, A2.pin3, Q9.B, 330Ω_9.Pin_0, Q10.B, 330Ω_10.Pin_0, Q11.B, 330Ω_11.Pin_0, Q12.B, 330Ω_12.Pin_0, Q13.B, 330Ω_13.Pin_0, Q14.B, 330Ω_14.Pin_0, Q15.B, 330Ω_15.Pin_0, Q16.B, 330Ω_16.Pin_0, 10uF.-, 10nF.-
  N4: 4_7kΩ.Pin_0, Q1.C, I2C_MCP_23017.VDD, I2C_MCP_23017.RESET, Q2.C, 4_7kΩ_2.Pin_0, Q4.C, Q3.C, 1kΩ.Pin_0, 4_7kΩ_3.Pin_0, Q5.C, Q8.C, Q6.C, Q7.C, 4_7kΩ_4.Pin_0, 4_7kΩ_5.Pin_0, 4_7kΩ_6.Pin_0, 4_7kΩ_7.Pin_0, OUT.pin5, IN.pin5, A0.pin1, A1.pin1, A2.pin1, 10KΩ.Pin_1, 10KΩ_2.Pin_1, 10KΩ_3.Pin_1, Q9.C, 4_7kΩ_8.Pin_1, Q10.C, 4_7kΩ_9.Pin_1, Q11.C, 4_7kΩ_10.Pin_1, Q12.C, 4_7kΩ_11.Pin_1, Q13.C, 4_7kΩ_12.Pin_1, Q14.C, 4_7kΩ_13.Pin_1, Q15.C, 4_7kΩ_14.Pin_1, Q16.C, 4_7kΩ_15.Pin_1, 10uF.+, 10nF.+
  N5: I2C_MCP_23017.GPB1, Q2.E, LED10.anode, 4_7kΩ_2.Pin_1
  N6: I2C_MCP_23017.GPB2, Q3.E, LED11.anode, 1kΩ.Pin_1
  N7: I2C_MCP_23017.GPB3, Q4.E, LED12.anode, 4_7kΩ_3.Pin_1
  N8: I2C_MCP_23017.GPB4, Q5.E, LED13.anode, 4_7kΩ_4.Pin_1
  N9: I2C_MCP_23017.GPB5, Q6.E, LED14.anode, 4_7kΩ_7.Pin_1
  N10: I2C_MCP_23017.GPB6, Q7.E, LED15.anode, 4_7kΩ_5.Pin_1
  N11: I2C_MCP_23017.GPB7, Q8.E, LED16.anode, 4_7kΩ_6.Pin_1
  N12: I2C_MCP_23017.SCL, OUT.pin3, IN.pin3, 10KΩ_2.Pin_0
  N13: I2C_MCP_23017.SDA, OUT.pin4, IN.pin4, 10KΩ_3.Pin_0
  N14: I2C_MCP_23017.A0, A0.pin2
  N15: I2C_MCP_23017.A1, A1.pin2
  N16: I2C_MCP_23017.A2, A2.pin2
  N17: I2C_MCP_23017.INTB, INT.pin1
  N18: I2C_MCP_23017.INTA, INT.pin3
  N19: I2C_MCP_23017.GPA0, Q16.E, LED8.cathode, 4_7kΩ_15.Pin_0
  N20: I2C_MCP_23017.GPA1, Q15.E, LED7.cathode, 4_7kΩ_14.Pin_0
  N21: I2C_MCP_23017.GPA2, Q14.E, LED6.cathode, 4_7kΩ_13.Pin_0
  N22: I2C_MCP_23017.GPA3, Q13.E, LED5.cathode, 4_7kΩ_12.Pin_0
  N23: I2C_MCP_23017.GPA4, Q12.E, LED4.cathode, 4_7kΩ_11.Pin_0
  N24: I2C_MCP_23017.GPA5, Q11.E, LED3_2.cathode, 4_7kΩ_10.Pin_0
  N25: I2C_MCP_23017.GPA6, Q10.E, LED3.cathode, 4_7kΩ_9.Pin_0
  N26: I2C_MCP_23017.GPA7, Q9.E, LED1.cathode, 4_7kΩ_8.Pin_0
  N27: LED10.cathode, 330Ω_2.Pin_1
  N28: LED11.cathode, 330Ω_3.Pin_1
  N29: LED12.cathode, 330Ω_4.Pin_1
  N30: LED16.cathode, 330Ω_8.Pin_1
  N31: LED13.cathode, 330Ω_5.Pin_1
  N32: LED15.cathode, 330Ω_7.Pin_1
  N33: LED14.cathode, 330Ω_6.Pin_1
  N34: OUT.pin2, IN.pin2, 10KΩ.Pin_0, INT.pin2
  N35: LED1.anode, 330Ω_9.Pin_1
  N36: LED3.anode, 330Ω_10.Pin_1
  N37: LED3_2.anode, 330Ω_11.Pin_1
  N38: LED4.anode, 330Ω_12.Pin_1
  N39: LED5.anode, 330Ω_13.Pin_1
  N40: LED6.anode, 330Ω_14.Pin_1
  N41: LED7.anode, 330Ω_15.Pin_1
  N42: LED8.anode, 330Ω_16.Pin_1

notes:
  SCL
  SDA
  INT
  VCC
  GND
  0
  1
  A
  B
  VSS

custom parts:
  MCP23017 I2C I/O Expander: The MCP23017 uses two i2c pins (these can be shared with other i2c devices), and in exchange gives you 16 general purpose pins. You can set each of 16 pins to be input, output, input with a pullup or open drain. There's even the ability to get an interrupt via an external pin when any of the inputs change so you don't have to keep polling the chip.
