# Fritzing sketch I2C NodeMCU Master (saved by Fritzing 0.9.3b)
circuit board: 5.5cm x 3.5cm
perfboards: 1

parts:
  Power_In = female pin header, 2 pins [form="♀ (female)"]
  J1 = female pin header, 5 pins [form="♀ (female)"]
  10uF = Electrolytic Capacitor [capacitance=1µF package="100 mil [THT, electrolytic]"]
  U1 = NodeMCU V1.0

nets:
  N1: Power_In.pin1, J1.pin1, 10uF.+, U1.3V3
  N2: Power_In.pin2, J1.pin5, 10uF.-, U1.GND
  N3: J1.pin2, U1.D1
  N4: J1.pin3, U1.D2
  N5: J1.pin4, U1.D5

notes:
  GND
  INT
  SCL
  SDA
  VCC (3.3V)
  5-12V
  3V3
  ESP 8266 Node MCU
  VCC

custom parts:
  NodeMCU V1.0: ESP8266 based NodeMCU
