# Fritzing sketch I2C Relais MCP 23017 (saved by Fritzing 0.9.3b)
circuit board: 6.4cm x 3.6cm
perfboards: 1

parts:
  Relais_1 = female pin header, 10 pins [form="♀ (female)"]
  Relais_2 = female pin header, 10 pins [form="♀ (female)"]
  A2 = female pin header, 3 pins [form="♀ (female)"]
  A1 = female pin header, 3 pins [form="♀ (female)"]
  A0 = female pin header, 3 pins [form="♀ (female)"]
  OUT = female pin header, 5 pins [form="♀ (female)"]
  R3_1KΩ = Resistor [tolerance=±5% resistance=1k package=THT]
  R1_1KΩ = Resistor [tolerance=±5% resistance=1k package=THT]
  R2_1KΩ = Resistor [tolerance=±5% resistance=1k package=THT]
  IN = female pin header, 5 pins [form="♀ (female)"]
  100nF = Ceramic Capacitor [capacitance=100nF package="100 mil [THT, multilayer]"]
  10uF = Electrolytic Capacitor [capacitance=10µF package="100 mil [THT, electrolytic]"]
  MCP_23017 = MCP23017 I2C I/O Expander

nets:
  N1: Relais_1.pin1, Relais_2.pin10, A2.pin3, A1.pin3, A0.pin3, OUT.pin1, IN.pin1, 100nF.1, 10uF.-, MCP_23017.VSS
  N2: Relais_1.pin2, MCP_23017.GPA7
  N3: Relais_1.pin3, MCP_23017.GPA6
  N4: Relais_1.pin4, MCP_23017.GPA5
  N5: Relais_1.pin5, MCP_23017.GPA4
  N6: Relais_1.pin6, MCP_23017.GPA3
  N7: Relais_1.pin7, MCP_23017.GPA2
  N8: Relais_1.pin8, MCP_23017.GPA1
  N9: Relais_1.pin9, MCP_23017.GPA0
  N10: Relais_1.pin10, Relais_2.pin1, A2.pin1, A1.pin1, A0.pin1, OUT.pin5, R3_1KΩ.Pin_1, R1_1KΩ.Pin_1, R2_1KΩ.Pin_1, IN.pin5, 100nF.0, 10uF.+, MCP_23017.VDD, MCP_23017.RESET
  N11: Relais_2.pin2, MCP_23017.GPB0
  N12: Relais_2.pin3, MCP_23017.GPB1
  N13: Relais_2.pin4, MCP_23017.GPB2
  N14: Relais_2.pin5, MCP_23017.GPB3
  N15: Relais_2.pin6, MCP_23017.GPB4
  N16: Relais_2.pin7, MCP_23017.GPB5
  N17: Relais_2.pin8, MCP_23017.GPB6
  N18: Relais_2.pin9, MCP_23017.GPB7
  N19: A2.pin2, MCP_23017.A2
  N20: A1.pin2, MCP_23017.A1
  N21: A0.pin2, MCP_23017.A0
  N22: OUT.pin2, R1_1KΩ.Pin_0, IN.pin2, MCP_23017.INTA
  N23: OUT.pin3, R2_1KΩ.Pin_0, IN.pin3, MCP_23017.SCL
  N24: OUT.pin4, R3_1KΩ.Pin_0, IN.pin4, MCP_23017.SDA

notes:
  VCC
  SDA
  SCL
  INT
  GND
  P01
  P08
  P16
  P09
  01
  08
  16
  09
  0
  1
  INTA

custom parts:
  MCP23017 I2C I/O Expander: The MCP23017 uses two i2c pins (these can be shared with other i2c devices), and in exchange gives you 16 general purpose pins. You can set each of 16 pins to be input, output, input with a pullup or open drain. There's even the ability to get an interrupt via an external pin when any of the inputs change so you don't have to keep polling the chip.
